# Fritzing sketch FHIReButton (saved by Fritzing 0.9.4)
breadboards: 2

parts:
  U1 = NodeMCU V1.0
  LED1 = LED - 3mm [color="Red (633nm)" package="3 mm [THT]"]
  LED2 = LED - 3mm [color="Yellow (585nm)" package="3 mm [THT]"]
  LED3 = LED - 3mm [color="Blue (470nm)" package="3 mm [THT]"]
  VCC1 = Battery
  SW1 = DIP Switch 4 Position [package=dipswitch-04]
  S1 = SPST Switch [package=switch-spdt]
  R6 = Resistor [tolerance=±5% resistance=220 package="0805 [SMD]"]
  R7 = Bussed4 Resistor-4 (SIP-5) [package=SIP-5]
  R8 = Bussed4 Resistor-4 (SIP-5) [package=SIP-5]

nets:
  N1: U1.D1, SW1.1, R7.Pin_1
  N2: U1.D2, SW1.2, R7.Pin_2
  N3: U1.3V3, U1.SD3, VCC1.+, SW1.5, SW1.6, SW1.7, SW1.8, S1.O, S1.P, S1.S, R6.Pin_0
  N4: U1.GND, VCC1.-, R6.Pin_1, R7.Pin_0, R8.Pin_0
  N5: U1.D5, SW1.3, R7.Pin_3
  N6: U1.D6, SW1.4, R7.Pin_4
  N7: U1.D8, LED1.anode
  N8: U1.RX, LED2.anode
  N9: U1.TX, LED3.anode
  N10: LED1.cathode, R8.Pin_1
  N11: LED2.cathode, R8.Pin_2
  N12: LED3.cathode, R8.Pin_3

notes:
  Designed by Davide Toldo
  2020

custom parts:
  NodeMCU V1.0: ESP8266 based NodeMCU
  Bussed4 Resistor-4 (SIP-5): A resistor array is a single package which contains more than one resistor. They are typically used for convenience when several resistors are needed together in the same place in a circuit.
  Bussed4 Resistor-4 (SIP-5): A resistor array is a single package which contains more than one resistor. They are typically used for convenience when several resistors are needed together in the same place in a circuit.
