# Fritzing sketch covid-button-perfboard (saved by Fritzing 0.9.5d)
perfboards: 1

parts:
  U1 = NodeMCU V1.0
  LED1 = LED - 3mm [color="Red (633nm)" package="3 mm [THT]"]
  LED2 = LED - 3mm [color="Yellow (592nm)" package="3 mm [THT]"]
  LED3 = LED - 3mm [color="Blue (430nm)" package="3 mm [THT]"]
  R1 = Bussed4 Resistor-4 (SIP-5) [package=SIP-5]
  SW1 = DIP Switch 4 Position [package=dipswitch-04]
  R2 = Bussed4 Resistor-4 (SIP-5) [package=SIP-5]
  S2 = SPST Switch [package=switch-spdt]
  R3 = Resistor [tolerance=±5% resistance=4700 package=THT]
  VCC2 = Battery

nets:
  N1: U1.D1, SW1.1, R2.Pin_1
  N2: U1.D2, SW1.2, R2.Pin_2
  N3: U1.3V3, SW1.5, SW1.6, SW1.7, SW1.8, S2.O
  N4: U1.GND, R1.Pin_0, R2.Pin_0, R3.Pin_0, VCC2.-
  N5: U1.D5, SW1.3, R2.Pin_3
  N6: U1.D6, SW1.4, R2.Pin_4
  N7: U1.D8, LED3.anode
  N8: U1.RX, LED2.anode
  N9: U1.TX, LED1.anode
  N10: U1.Vin, VCC2.+
  N11: U1.SD3, S2.S, R3.Pin_1
  N12: LED1.cathode, R1.Pin_1
  N13: LED2.cathode, R1.Pin_2
  N14: LED3.cathode, R1.Pin_3

custom parts:
  NodeMCU V1.0: ESP8266 based NodeMCU
  Bussed4 Resistor-4 (SIP-5): A resistor array is a single package which contains more than one resistor. They are typically used for convenience when several resistors are needed together in the same place in a circuit.
  Bussed4 Resistor-4 (SIP-5): A resistor array is a single package which contains more than one resistor. They are typically used for convenience when several resistors are needed together in the same place in a circuit.
